// Logisim project ex5.circ as structural Verilog: 5 circuits, main circuit rotr
module rotr (
  input  [15:0] A,
  input  [3:0] B,
  output [15:0] Out1
);

  wire [3:0] subtractor_1_out;
  wire [15:0] multiplexer_1_out, multiplexer_2_out, multiplexer_3_out, multiplexer_4_out, multiplexer_5_out,
       multiplexer_6_out, multiplexer_7_out, multiplexer_8_out, rot1_1_out_2, rot1_2_out_2, rot2_1_out_2,
       rot2_2_out_2, rot4_1_out_2, rot4_2_out_2, rot8_1_out_2, rot8_2_out_2;

  // OR_Gate or_1 is placed but not wired
  Multiplexer #(.width(16), .enable("false")) multiplexer_1 (
    .in0(A), .in1(rot8_1_out_2), .out(multiplexer_1_out), .sel(B[3]));
  rot8 rot8_1 (.in_1(A), .out_2(rot8_1_out_2));
  Subtractor #(.width(4)) subtractor_1 (.a(4'b0000), .b(B), .out(subtractor_1_out));  // open: bin, bout
  rot4 rot4_1 (.in_1(multiplexer_1_out), .out_2(rot4_1_out_2));
  Multiplexer #(.width(16), .enable("false")) multiplexer_2 (
    .in0({A[0], A[1], A[2], A[3], A[4], A[5], A[6], A[7], A[8], A[9], A[10], A[11], A[12], A[13], A[14], A[15]}),
    .in1(rot8_2_out_2), .out(multiplexer_2_out), .sel(subtractor_1_out[3]));
  rot8 rot8_2 (
    .in_1({A[0], A[1], A[2], A[3], A[4], A[5], A[6], A[7], A[8], A[9], A[10], A[11], A[12], A[13], A[14], A[15]}),
    .out_2(rot8_2_out_2));
  Multiplexer #(.width(16), .enable("false")) multiplexer_3 (
    .in0(multiplexer_1_out), .in1(rot4_1_out_2), .out(multiplexer_3_out), .sel(B[2]));
  Multiplexer #(.width(16), .enable("false")) multiplexer_4 (
    .in0(multiplexer_2_out), .in1(rot4_2_out_2), .out(multiplexer_4_out), .sel(subtractor_1_out[2]));
  rot4 rot4_2 (.in_1(multiplexer_2_out), .out_2(rot4_2_out_2));
  Multiplexer #(.width(16), .enable("false")) multiplexer_5 (
    .in0(multiplexer_3_out), .in1(rot2_1_out_2), .out(multiplexer_5_out), .sel(B[1]));
  rot2 rot2_1 (.in_1(multiplexer_3_out), .out_2(rot2_1_out_2));
  rot2 rot2_2 (.in_1(multiplexer_4_out), .out_2(rot2_2_out_2));
  Multiplexer #(.width(16), .enable("false")) multiplexer_6 (
    .in0(multiplexer_5_out), .in1(rot1_1_out_2), .out(multiplexer_6_out), .sel(B[0]));
  rot1 rot1_1 (.in_1(multiplexer_5_out), .out_2(rot1_1_out_2));
  Multiplexer #(.width(16), .enable("false")) multiplexer_7 (
    .in0(multiplexer_4_out), .in1(rot2_2_out_2), .out(multiplexer_7_out), .sel(subtractor_1_out[1]));
  Multiplexer #(.width(16), .enable("false")) multiplexer_8 (
    .in0(multiplexer_7_out), .in1(rot1_2_out_2), .out(multiplexer_8_out), .sel(subtractor_1_out[0]));
  rot1 rot1_2 (.in_1(multiplexer_7_out), .out_2(rot1_2_out_2));
  or or_2 (Out1[0], multiplexer_6_out[0], multiplexer_8_out[15]);
  or or_3 (Out1[1], multiplexer_6_out[1], multiplexer_8_out[14]);
  or or_4 (Out1[2], multiplexer_6_out[2], multiplexer_8_out[13]);
  or or_5 (Out1[3], multiplexer_6_out[3], multiplexer_8_out[12]);
  or or_6 (Out1[4], multiplexer_6_out[4], multiplexer_8_out[11]);
  or or_7 (Out1[5], multiplexer_6_out[5], multiplexer_8_out[10]);
  or or_8 (Out1[6], multiplexer_6_out[6], multiplexer_8_out[9]);
  or or_9 (Out1[7], multiplexer_6_out[7], multiplexer_8_out[8]);
  or or_10 (Out1[8], multiplexer_6_out[8], multiplexer_8_out[7]);
  or or_11 (Out1[9], multiplexer_6_out[9], multiplexer_8_out[6]);
  or or_12 (Out1[10], multiplexer_6_out[10], multiplexer_8_out[5]);
  or or_13 (Out1[11], multiplexer_6_out[11], multiplexer_8_out[4]);
  or or_14 (Out1[12], multiplexer_6_out[12], multiplexer_8_out[3]);
  or or_15 (Out1[13], multiplexer_6_out[13], multiplexer_8_out[2]);
  or or_16 (Out1[14], multiplexer_6_out[14], multiplexer_8_out[1]);
  or or_17 (Out1[15], multiplexer_6_out[15], multiplexer_8_out[0]);

  // Notes on the sheet:
  //   PUT CIRCUITRY HERE
endmodule

module rot8 (
  input  [15:0] in_1,
  output [15:0] out_2
);


  assign out_2 = {{8{1'b0}}, in_1[15:8]};

  // Notes on the sheet:
  //   PUT CIRCUITRY HERE
endmodule

module rot4 (
  input  [15:0] in_1,
  output [15:0] out_2
);


  assign out_2 = {4'b0000, in_1[15:4]};

  // Notes on the sheet:
  //   PUT CIRCUITRY HERE
endmodule

module rot2 (
  input  [15:0] in_1,
  output [15:0] out_2
);


  assign out_2 = {2'b00, in_1[15:2]};

  // Notes on the sheet:
  //   PUT CIRCUITRY HERE
endmodule

module rot1 (
  input  [15:0] in_1,
  output [15:0] out_2
);


  assign out_2 = {1'b0, in_1[15:1]};

  // Notes on the sheet:
  //   PUT CIRCUITRY HERE
endmodule
