// Logisim project alu.circ as structural Verilog: 2 circuits, main circuit alu
module alu (
  input  [31:0] A,
  input  [31:0] B,
  input  [3:0] ALUSel,
  output [31:0] Result
);

  wire adder_7_cout, xor_2_out;
  wire [0:0] slt7;
  wire [31:0] A2s, add0, adder_1_out, adder_2_out, adder_3_out, adder_4_out, adder_5_out, and1, B2s,
       bit_extender_1_out, divu8, mul10, mulh14, mulhu11, multiplexer_2_out, multiplexer_3_out,
       multiplier_1_cout, multiplier_1_out, multiplier_2_out, not_1_out, not_2_out, not_3_out, not_4_out,
       not_5_out, not_6_out, or2, remu9, sll6, sra5, srl4, sub12, xor3;

  assign not_1_out = ~A;  // NOT_Gate not_1, 32 bits wide
  assign not_2_out = ~A;  // NOT_Gate not_2, 32 bits wide
  assign not_3_out = ~B;  // NOT_Gate not_3, 32 bits wide
  Adder #(.width(32)) adder_1 (.a(not_1_out), .b(32'h1), .out(adder_1_out));  // open: cin, cout
  Adder #(.width(32)) adder_2 (.a(not_2_out), .b(32'h1), .out(adder_2_out));  // open: cin, cout
  Adder #(.width(32)) adder_3 (.a(32'h1), .b(not_3_out), .out(adder_3_out));  // open: cin, cout
  Multiplexer #(.width(32), .enable("false")) multiplexer_1 (.in0(A), .in1(adder_1_out), .out(A2s), .sel(A[31]));
  Multiplexer #(.width(32), .enable("false")) multiplexer_2 (
    .in0(A), .in1(adder_2_out), .out(multiplexer_2_out), .sel(A[31]));
  Multiplexer #(.width(32), .enable("false")) multiplexer_3 (
    .in0(B), .in1(adder_3_out), .out(multiplexer_3_out), .sel(B[31]));
  assign not_4_out = ~B;  // NOT_Gate not_4, 32 bits wide
  Multiplier #(.width(32)) multiplier_1 (
    .a(multiplexer_2_out), .b(multiplexer_3_out), .out(multiplier_1_out), .cout(multiplier_1_cout));  // open: cin
  assign not_5_out = ~multiplier_1_cout;  // NOT_Gate not_5, 32 bits wide
  Comparator #(.width(32)) comparator_1 (.a(A), .b(B), .lt(slt7[0]));  // open: gt, eq
  Adder #(.width(32)) adder_4 (.a(not_4_out), .b(32'h1), .out(adder_4_out));  // open: cin, cout
  assign not_6_out = ~multiplier_1_out;  // NOT_Gate not_6, 32 bits wide
  Adder #(.width(32)) adder_5 (.a(bit_extender_1_out), .b(not_5_out), .out(adder_5_out));  // open: cin, cout
  Adder #(.width(32)) adder_6 (.a(A), .b(B), .out(add0));  // open: cin, cout
  assign and1 = A & B;  // AND_Gate and_1, 32 bits wide
  assign or2 = A | B;  // OR_Gate or_1, 32 bits wide
  assign xor3 = A ^ B;  // XOR_Gate xor_1, 32 bits wide
  Shifter #(.width(32), .shift("lr")) shifter_1 (.in(A), .\dist (B[4:0]), .out(srl4));
  Shifter #(.width(32), .shift("ar")) shifter_2 (.in(A), .\dist (B[4:0]), .out(sra5));
  Shifter #(.width(32)) shifter_3 (.in(A), .\dist (B[4:0]), .out(sll6));
  Multiplexer #(.width(32), .enable("false")) multiplexer_4 (.in0(B), .in1(adder_4_out), .out(B2s), .sel(B[31]));
  Adder #(.width(32)) adder_7 (.a(32'h1), .b(not_6_out), .cout(adder_7_cout));  // open: out, cin
  Multiplexer #(.width(32), .enable("false")) multiplexer_5 (
    .in0(multiplier_1_cout), .in1(adder_5_out), .out(mulh14), .sel(xor_2_out));
  xor xor_2 (xor_2_out, A[31], B[31]);
  assign bit_extender_1_out = {{31{adder_7_cout}}, adder_7_cout};  // Bit_Extender bit_extender_1
  Multiplier #(.width(32)) multiplier_2 (.a(B), .b(divu8), .out(multiplier_2_out));  // open: cin, cout
  Divider #(.width(32)) divider_1 (.a(A), .b(B), .out(divu8));  // open: upper, rem
  Subtractor #(.width(32)) subtractor_1 (.a(A), .b(multiplier_2_out), .out(remu9));  // open: bin, bout
  Multiplier #(.width(32)) multiplier_3 (.a(A), .b(B), .out(mul10), .cout(mulhu11));  // open: cin
  Subtractor #(.width(32)) subtractor_2 (.a(A), .b(B), .out(sub12));  // open: bin, bout
  Multiplexer #(.select(4), .width(32), .enable("false")) multiplexer_6 (
    .in0(add0), .in1(and1), .in2(or2), .in3(xor3), .in4(srl4), .in5(sra5), .in6(sll6),
    .in7({{31{1'b0}}, slt7[0]}), .in8(divu8), .in9(remu9), .in10(mul10), .in11(mulhu11), .in12(sub12),
    .in13(B), .in14(mulh14), .out(Result), .sel(ALUSel));  // open: in15

  // Other names for the same wires on the sheet: bsel13[31:0] = B

  // Notes on the sheet:
  //   INPUTS to your circuit
  //   DON'T CHANGE THE LOCATIONS OF THE INPUTS AND OUTPUTS!
  //   OUTPUT from your circuit
endmodule

module test (
  input  [15:0] in_1,
  input  [15:0] in_2,
  input  [15:0] in_3,
  output [15:0] out_4,
  output [15:0] out_5,
  output [15:0] out_6
);

  // Probe on in_2
  // Probe on in_3
  Negator #(.width(16)) negator_1 (.in(in_1), .out(out_4));
  Multiplier #(.width(16)) multiplier_1 (.a(in_2), .b(in_3), .out(out_5), .cout(out_6));  // open: cin
  // Probe on out_5
  // Probe on out_6
endmodule
